# Fritzing sketch schematic (saved by Fritzing 0.9.3b)
breadboards: 1

parts:
  Part1 = LightBlue Bean
  J1 = Piezo Speaker

nets:
  N1: Part1.D4/MISO, J1.pin1
  N2: Part1.D3/MOSI, Part1.D2, Part1.D1, Part1.GND, J1.pin2
